// Logisim project 74153Sixteen_to_One.circ as structural Verilog: 1 circuit, main circuit main
module main (
  input  A_Zero,
  input  C_Two,
  input  D_Three,
  input  B_One,
  output F
);

  wire n74153_1_pin1, n74153_1_pin3, n74153_1_pin4, n74153_1_pin5, n74153_1_pin6, n74153_1_pin7,
       n74153_1_pin9, n74153_1_pin10, n74153_1_pin11, n74153_1_pin12, n74153_1_pin13, n74153_1_pin15,
       n74153_2_pin1, n74153_2_pin3, n74153_2_pin4, n74153_2_pin5, n74153_2_pin6, n74153_2_pin7,
       n74153_2_pin9, n74153_2_pin10, n74153_2_pin11, n74153_2_pin12, n74153_2_pin13, n74153_2_pin15,
       n74153_3_pin1, n74153_3_pin15;

  _74153 #(.ShowInternalStructure("true")) u_74153_1 (
    .pin1(n74153_1_pin1), .pin2(B_One), .pin3(n74153_1_pin3), .pin4(n74153_1_pin4), .pin5(n74153_1_pin5),
    .pin6(n74153_1_pin6), .pin7(n74153_1_pin7), .pin15(n74153_1_pin15), .pin14(A_Zero),
    .pin13(n74153_1_pin13), .pin12(n74153_1_pin12), .pin11(n74153_1_pin11), .pin10(n74153_1_pin10),
    .pin9(n74153_1_pin9));
  _74153 #(.ShowInternalStructure("true")) u_74153_2 (
    .pin1(n74153_2_pin1), .pin2(B_One), .pin3(n74153_2_pin3), .pin4(n74153_2_pin4), .pin5(n74153_2_pin5),
    .pin6(n74153_2_pin6), .pin7(n74153_2_pin7), .pin15(n74153_2_pin15), .pin14(A_Zero),
    .pin13(n74153_2_pin13), .pin12(n74153_2_pin12), .pin11(n74153_2_pin11), .pin10(n74153_2_pin10),
    .pin9(n74153_2_pin9));
  _74153 #(.ShowInternalStructure("true")) u_74153_3 (
    .pin1(n74153_3_pin1), .pin2(D_Three), .pin3(n74153_2_pin9), .pin4(n74153_2_pin7), .pin5(n74153_1_pin9),
    .pin6(n74153_1_pin7), .pin7(F), .pin15(n74153_3_pin15), .pin14(C_Two));  // open: pin13, pin12, pin11, pin10, pin9
  // also tied to GND on the sheet: {n74153_1_pin1, n74153_1_pin15, n74153_1_pin3, n74153_1_pin4, n74153_1_pin12, n74153_1_pin10, n74153_2_pin1, n74153_2_pin15, n74153_2_pin3, n74153_2_pin12, n74153_2_pin5, n74153_2_pin6, n74153_3_pin1, n74153_3_pin15}
  // also tied to VCC on the sheet: {n74153_1_pin13, n74153_1_pin5, n74153_1_pin11, n74153_1_pin6, n74153_2_pin13, n74153_2_pin4, n74153_2_pin11, n74153_2_pin10}
endmodule
