// Logisim project Homework_YiBushixu.circ as structural Verilog: 1 circuit, main circuit main
module main (
);

  wire and_1_out, clock_1_out, JK1_q, JK2_q, JK3_qn;

  and and_1 (and_1_out, JK3_qn, JK2_q);
  J_K_Flip_Flop #(.trigger("falling")) JK3 (
    .J(and_1_out), .K(1'b1), .clk(JK1_q), .Qn(JK3_qn));  // open: Q, preset, reset
  J_K_Flip_Flop #(.trigger("falling")) JK2 (.J(JK3_qn), .K(1'b1), .clk(JK1_q), .Q(JK2_q));  // open: Qn, preset, reset
  J_K_Flip_Flop #(.trigger("falling")) JK1 (
    .J(1'b1), .K(1'b1), .clk(clock_1_out), .Q(JK1_q));  // open: Qn, preset, reset
  Clock clock_1 (.out(clock_1_out));
endmodule
