// Logisim project PasswordCheck.circ as structural Verilog: 1 circuit, main circuit main
module main (
);

  wire inputKey_p1, inputKey_p2, inputKey_p3, inputKey_p4, nor_1_out, Set_p1, Set_p2, Set_p3, Set_p4,
       undriven, undriven_2, undriven_3, Verify_out, xor_1_out, xor_2_out, xor_3_out, xor_4_out;
  wire [3:0] d_ff_1_q;

  // DipSwitch #(.number(4)) Set: pin names not known; wires that end beside it: Set_p1, Set_p2, Set_p3, Set_p4, Set_p1
  Button Verify (.out(Verify_out));
  // DipSwitch #(.number(4)) inputKey: pin names not known; wires that end beside it: inputKey_p1, inputKey_p2, inputKey_p3, inputKey_p4
  D_Flip_Flop d_ff_1 (.D(Set_p1), .clk(Verify_out), .Q(d_ff_1_q[0]), .reset(undriven));  // open: Qn, preset
  D_Flip_Flop d_ff_2 (
    .D(Set_p2), .clk(Verify_out), .Q(d_ff_1_q[1]), .preset(undriven), .reset(undriven_2));  // open: Qn
  D_Flip_Flop d_ff_3 (
    .D(Set_p3), .clk(Verify_out), .Q(d_ff_1_q[2]), .preset(undriven_2), .reset(undriven_3));  // open: Qn
  D_Flip_Flop d_ff_4 (.D(Set_p4), .clk(Verify_out), .Q(d_ff_1_q[3]), .preset(undriven_3));  // open: Qn, reset
  xor xor_1 (xor_1_out, inputKey_p1, d_ff_1_q[0]);
  xor xor_2 (xor_2_out, inputKey_p2, d_ff_1_q[1]);
  xor xor_3 (xor_3_out, inputKey_p3, d_ff_1_q[2]);
  xor xor_4 (xor_4_out, inputKey_p4, d_ff_1_q[3]);
  Hex_Digit_Display #(.decimalPoint("false")) outputKey (.value(d_ff_1_q));
  nor nor_1 (nor_1_out, xor_1_out, xor_2_out, xor_3_out, xor_4_out);
  LED TrueOrNot (.in(nor_1_out));
endmodule
