// Logisim project TrafficLight.circ as structural Verilog: 8 circuits, main circuit Mode_Switch
module main (
  input  in_1,
  input  in_2
);

  wire and_1_out, bcd_to_7seg_1_a, bcd_to_7seg_1_b, bcd_to_7seg_1_c, bcd_to_7seg_1_d, bcd_to_7seg_1_e,
       bcd_to_7seg_1_f, bcd_to_7seg_1_g, bcd_to_7seg_2_a, bcd_to_7seg_2_b, bcd_to_7seg_2_c, bcd_to_7seg_2_d,
       bcd_to_7seg_2_e, bcd_to_7seg_2_f, bcd_to_7seg_2_g, bcd_to_7seg_3_a, bcd_to_7seg_3_b, bcd_to_7seg_3_c,
       bcd_to_7seg_3_d, bcd_to_7seg_3_e, bcd_to_7seg_3_f, bcd_to_7seg_3_g, bcd_to_7seg_4_a, bcd_to_7seg_4_b,
       bcd_to_7seg_4_c, bcd_to_7seg_4_d, bcd_to_7seg_4_e, bcd_to_7seg_4_f, bcd_to_7seg_4_g, clock_1_out,
       mode_switch_1_s_emer, mode_switch_1_s_night_flash, mode_switch_1_s_norm, Q_0_qn, Q_1_qn, Q_2_qn,
       Q_3_qn, Q_4_qn, Q_5_qn, Q_6_qn, traffic_logic_1_ewgreen, traffic_logic_1_ewred,
       traffic_logic_1_ewyellow, traffic_logic_1_nsgreen, traffic_logic_1_nsred, traffic_logic_1_nsyellow;
  wire [3:0] ewsecond_1_ones, ewsecond_1_tens, nssecond_1_ones, nssecond_1_tens;
  wire [6:0] Q_0_q;

  Clock clock_1 (.out(clock_1_out));
  D_Flip_Flop Q_0 (.D(Q_0_qn), .clk(clock_1_out), .Q(Q_0_q[0]), .Qn(Q_0_qn), .preset(1'b0), .reset(and_1_out));
  D_Flip_Flop Q_1 (.D(Q_1_qn), .clk(Q_0_qn), .Q(Q_0_q[1]), .Qn(Q_1_qn), .reset(and_1_out));  // open: preset
  Mode_Switch mode_switch_1 (
    .Emergency(in_1), .Night(in_2), .Sys_Clk(clock_1_out), .S_Emer(mode_switch_1_s_emer),
    .S_Night_Flash(mode_switch_1_s_night_flash), .S_Norm(mode_switch_1_s_norm));
  and and_1 (and_1_out, Q_0_q[6], Q_0_q[4]);
  D_Flip_Flop Q_2 (.D(Q_2_qn), .clk(Q_1_qn), .Q(Q_0_q[2]), .Qn(Q_2_qn), .reset(and_1_out));  // open: preset
  D_Flip_Flop Q_3 (.D(Q_3_qn), .clk(Q_2_qn), .Q(Q_0_q[3]), .Qn(Q_3_qn), .reset(and_1_out));  // open: preset
  NSSecond nssecond_1 (
    .x6(Q_0_q[6]), .x5(Q_0_q[5]), .x4(Q_0_q[4]), .x3(Q_0_q[3]), .x2(Q_0_q[2]), .x1(Q_0_q[1]), .x0(Q_0_q[0]),
    .Tens(nssecond_1_tens), .Ones(nssecond_1_ones));
  EWSecond ewsecond_1 (
    .x6(Q_0_q[6]), .x5(Q_0_q[5]), .x4(Q_0_q[4]), .x3(Q_0_q[3]), .x2(Q_0_q[2]), .x1(Q_0_q[1]), .x0(Q_0_q[0]),
    .Tens(ewsecond_1_tens), .Ones(ewsecond_1_ones));
  D_Flip_Flop Q_4 (.D(Q_4_qn), .clk(Q_3_qn), .Q(Q_0_q[4]), .Qn(Q_4_qn), .reset(and_1_out));  // open: preset
  LED led_1 (.in(traffic_logic_1_ewred));
  Traffic_Logic traffic_logic_1 (
    .Count(Q_0_q), .S_Norm(mode_switch_1_s_norm), .S_Emer(mode_switch_1_s_emer),
    .S_Night_Flash(mode_switch_1_s_night_flash), .EWRed(traffic_logic_1_ewred),
    .NSRed(traffic_logic_1_nsred), .EWYellow(traffic_logic_1_ewyellow), .NSYellow(traffic_logic_1_nsyellow),
    .EWGreen(traffic_logic_1_ewgreen), .NSGreen(traffic_logic_1_nsgreen));
  LED led_2 (.in(traffic_logic_1_nsred));
  LED led_3 (.in(traffic_logic_1_ewyellow));
  LED led_4 (.in(traffic_logic_1_nsyellow));
  LED led_5 (.in(traffic_logic_1_ewgreen));
  LED led_6 (.in(traffic_logic_1_nsgreen));
  BCD_to_7Seg bcd_to_7seg_1 (
    .Enable(mode_switch_1_s_norm), .Ai(nssecond_1_tens[3]), .Bi(nssecond_1_tens[2]), .Ci(nssecond_1_tens[1]),
    .Di(nssecond_1_tens[0]), .a(bcd_to_7seg_1_a), .b(bcd_to_7seg_1_b), .c(bcd_to_7seg_1_c),
    .d(bcd_to_7seg_1_d), .e(bcd_to_7seg_1_e), .f(bcd_to_7seg_1_f), .g(bcd_to_7seg_1_g));
  BCD_to_7Seg bcd_to_7seg_2 (
    .Enable(mode_switch_1_s_norm), .Ai(nssecond_1_ones[3]), .Bi(nssecond_1_ones[2]), .Ci(nssecond_1_ones[1]),
    .Di(nssecond_1_ones[0]), .a(bcd_to_7seg_2_a), .b(bcd_to_7seg_2_b), .c(bcd_to_7seg_2_c),
    .d(bcd_to_7seg_2_d), .e(bcd_to_7seg_2_e), .f(bcd_to_7seg_2_f), .g(bcd_to_7seg_2_g));
  BCD_to_7Seg bcd_to_7seg_3 (
    .Enable(mode_switch_1_s_norm), .Ai(ewsecond_1_tens[3]), .Bi(ewsecond_1_tens[2]), .Ci(ewsecond_1_tens[1]),
    .Di(ewsecond_1_tens[0]), .a(bcd_to_7seg_3_a), .b(bcd_to_7seg_3_b), .c(bcd_to_7seg_3_c),
    .d(bcd_to_7seg_3_d), .e(bcd_to_7seg_3_e), .f(bcd_to_7seg_3_f), .g(bcd_to_7seg_3_g));
  BCD_to_7Seg bcd_to_7seg_4 (
    .Enable(mode_switch_1_s_norm), .Ai(ewsecond_1_ones[3]), .Bi(ewsecond_1_ones[2]), .Ci(ewsecond_1_ones[1]),
    .Di(ewsecond_1_ones[0]), .a(bcd_to_7seg_4_a), .b(bcd_to_7seg_4_b), .c(bcd_to_7seg_4_c),
    .d(bcd_to_7seg_4_d), .e(bcd_to_7seg_4_e), .f(bcd_to_7seg_4_f), .g(bcd_to_7seg_4_g));
  D_Flip_Flop Q_5 (.D(Q_5_qn), .clk(Q_4_qn), .Q(Q_0_q[5]), .Qn(Q_5_qn), .reset(and_1_out));  // open: preset
  _7_Segment_Display u_7_segment_display_1 (
    .g(bcd_to_7seg_1_g), .f(bcd_to_7seg_1_f), .a(bcd_to_7seg_1_a), .b(bcd_to_7seg_1_b), .e(bcd_to_7seg_1_e),
    .d(bcd_to_7seg_1_d), .c(bcd_to_7seg_1_c));  // open: dp
  _7_Segment_Display u_7_segment_display_2 (
    .g(bcd_to_7seg_2_g), .f(bcd_to_7seg_2_f), .a(bcd_to_7seg_2_a), .b(bcd_to_7seg_2_b), .e(bcd_to_7seg_2_e),
    .d(bcd_to_7seg_2_d), .c(bcd_to_7seg_2_c));  // open: dp
  _7_Segment_Display u_7_segment_display_3 (
    .g(bcd_to_7seg_3_g), .f(bcd_to_7seg_3_f), .a(bcd_to_7seg_3_a), .b(bcd_to_7seg_3_b), .e(bcd_to_7seg_3_e),
    .d(bcd_to_7seg_3_d), .c(bcd_to_7seg_3_c));  // open: dp
  _7_Segment_Display u_7_segment_display_4 (
    .g(bcd_to_7seg_4_g), .f(bcd_to_7seg_4_f), .a(bcd_to_7seg_4_a), .b(bcd_to_7seg_4_b), .e(bcd_to_7seg_4_e),
    .d(bcd_to_7seg_4_d), .c(bcd_to_7seg_4_c));  // open: dp
  D_Flip_Flop Q_6 (.D(Q_6_qn), .clk(Q_5_qn), .Q(Q_0_q[6]), .Qn(Q_6_qn), .reset(and_1_out));  // open: preset
endmodule

module Mode_Switch (
  input  Emergency,
  input  Night,
  input  Sys_Clk,
  output S_Emer,
  output S_Night_Flash,
  output S_Norm
);

  wire not_1_out;

  not not_1 (not_1_out, Emergency);
  and and_1 (S_Night_Flash, not_1_out, Night, Sys_Clk);
  nor nor_1 (S_Norm, Emergency, Night);

  assign S_Emer = Emergency;
endmodule

module Traffic_Logic (
  input  [6:0] Count,
  input  S_Norm,
  input  S_Emer,
  input  S_Night_Flash,
  output EWRed,
  output NSRed,
  output EWYellow,
  output NSYellow,
  output EWGreen,
  output NSGreen
);

  wire and_1_out, and_2_out, and_3_out, and_4_out, and_5_out, and_6_out, and_7_out, and_8_out, and_9_out,
       and_10_out, and_11_out, and_12_out, and_13_out, and_14_out, and_15_out, and_16_out, and_17_out,
       and_18_out, and_19_out, and_20_out, and_21_out, and_22_out, and_23_out, not_1_out, not_2_out,
       not_3_out, not_4_out, not_5_out, not_6_out, not_7_out, not_8_out, not_9_out;

  not not_1 (not_1_out, Count[6]);
  not not_2 (not_2_out, Count[5]);
  not not_3 (not_3_out, Count[4]);
  not not_4 (not_4_out, Count[3]);
  not not_5 (not_5_out, Count[2]);
  not not_6 (not_6_out, Count[1]);
  not not_7 (not_7_out, Count[0]);
  not not_8 (not_8_out, S_Emer);
  not not_9 (not_9_out, S_Night_Flash);
  and and_1 (and_1_out, not_1_out, Count[5], Count[3], Count[0], S_Norm, not_9_out);
  and and_2 (and_2_out, not_1_out, Count[5], Count[3], Count[1], S_Norm, not_9_out);
  and and_3 (and_3_out, not_1_out, Count[5], Count[3], Count[2], S_Norm, not_9_out);
  and and_4 (and_4_out, not_1_out, Count[5], Count[4], S_Norm, not_9_out);
  and and_5 (and_5_out, Count[6], not_2_out, not_3_out, S_Norm, not_9_out);
  and and_6 (and_6_out, Count[6], not_2_out, not_4_out, not_5_out, not_6_out, not_7_out, S_Norm, not_9_out);
  and and_7 (and_7_out, not_1_out, not_2_out, S_Norm, not_9_out);
  and and_8 (and_8_out, not_1_out, not_3_out, not_4_out, S_Norm, not_9_out);
  and and_9 (and_9_out, not_1_out, not_3_out, not_5_out, not_6_out, not_7_out, S_Norm, not_9_out);
  and and_10 (and_10_out, not_8_out, S_Night_Flash);
  and and_11 (and_11_out, not_1_out, Count[5], not_3_out, not_4_out, Count[2], S_Norm, not_8_out);
  and and_12 (and_12_out, not_1_out, Count[5], not_3_out, Count[3], not_5_out, not_6_out, not_7_out, S_Norm, not_8_out);
  and and_13 (and_13_out, not_8_out, S_Night_Flash);
  and and_14 (and_14_out, Count[6], not_2_out, not_3_out, Count[3], Count[2], S_Norm, not_8_out);
  and and_15 (and_15_out, Count[6], not_2_out, Count[4], not_4_out, not_5_out, not_6_out, not_7_out, S_Norm, not_8_out);
  and and_16 (and_16_out, not_1_out, not_2_out, S_Norm, not_8_out, not_9_out);
  and and_17 (and_17_out, not_1_out, not_3_out, not_4_out, not_5_out, S_Norm, not_8_out, not_9_out);
  and and_18 (and_18_out, not_1_out, Count[5], Count[4], S_Norm, not_8_out, not_9_out);
  and and_19 (and_19_out, Count[6], not_2_out, not_3_out, not_5_out, S_Norm, not_8_out, not_9_out);
  and and_20 (and_20_out, not_1_out, Count[5], Count[3], Count[0], S_Norm, not_8_out, not_9_out);
  and and_21 (and_21_out, not_1_out, Count[5], Count[3], Count[1], S_Norm, not_8_out, not_9_out);
  and and_22 (and_22_out, not_1_out, Count[5], Count[3], Count[2], S_Norm, not_8_out, not_9_out);
  and and_23 (and_23_out, Count[6], not_2_out, not_3_out, not_4_out, S_Norm, not_8_out, not_9_out);
  or or_1 (EWRed, S_Emer, and_1_out, and_2_out, and_3_out, and_4_out, and_5_out, and_6_out);
  or or_2 (NSRed, S_Emer, and_7_out, and_8_out, and_9_out);
  or or_3 (EWYellow, and_10_out, and_11_out, and_12_out);
  or or_4 (NSYellow, and_13_out, and_14_out, and_15_out);
  or or_5 (EWGreen, and_16_out, and_17_out);
  or or_6 (NSGreen, and_18_out, and_19_out, and_20_out, and_21_out, and_22_out, and_23_out);
endmodule

module Display_Decoder (
  input  [6:0] Count,
  output [3:0] Tens,
  output [3:0] Ones
);

  Calc_Countdown calc_countdown_1 (
    .C5(Count[5]), .C4(Count[4]), .C3(Count[3]), .C2(Count[2]), .C1(Count[1]), .C0(Count[0]), .T2(Tens[2]),
    .T1(Tens[1]), .T0(Tens[0]), .G3(Ones[3]), .G2(Ones[2]), .G1(Ones[1]), .G0(Ones[0]));

  assign Tens[3] = 1'b0;
endmodule

module BCD_to_7Seg (
  input  Enable,
  input  Ai,
  input  Bi,
  input  Ci,
  input  Di,
  output a,
  output b,
  output c,
  output d,
  output e,
  output f,
  output g
);

  wire and_1_out, and_2_out, and_3_out, and_4_out, and_5_out, and_6_out, and_7_out, and_8_out, and_9_out,
       and_10_out, and_11_out, and_12_out, and_13_out, and_14_out, and_15_out, and_16_out, not_1_out,
       not_2_out, not_3_out, or_1_out, or_2_out, or_3_out, or_4_out, or_5_out, or_6_out, or_7_out;

  not not_1 (not_1_out, Bi);
  not not_2 (not_2_out, Ci);
  not not_3 (not_3_out, Di);
  and and_1 (and_1_out, not_1_out, not_3_out);
  and and_2 (and_2_out, Bi, Di);
  and and_3 (and_3_out, not_2_out, not_3_out);
  and and_4 (and_4_out, Ci, Di);
  or or_1 (or_1_out, not_2_out, Di, Bi);
  and and_5 (and_5_out, not_1_out, not_3_out);
  and and_6 (and_6_out, not_1_out, Ci);
  and and_7 (and_7_out, Bi, not_2_out, Di);
  and and_8 (and_8_out, Ci, not_3_out);
  and and_9 (and_9_out, not_1_out, not_3_out);
  and and_10 (and_10_out, Ci, not_3_out);
  and and_11 (and_11_out, not_2_out, not_3_out);
  and and_12 (and_12_out, Bi, not_2_out);
  and and_13 (and_13_out, Bi, not_3_out);
  and and_14 (and_14_out, not_1_out, Ci);
  and and_15 (and_15_out, Bi, not_2_out);
  and and_16 (and_16_out, Ci, not_3_out);
  or or_2 (or_2_out, and_1_out, Ci, and_2_out, Ai);
  and and_17 (b, Enable, or_3_out);
  or or_3 (or_3_out, not_1_out, and_3_out, and_4_out);
  and and_18 (c, Enable, or_1_out);
  or or_4 (or_4_out, and_5_out, and_6_out, and_7_out, and_8_out, Ai);
  and and_19 (e, Enable, or_5_out);
  or or_5 (or_5_out, and_9_out, and_10_out);
  or or_6 (or_6_out, and_11_out, and_12_out, and_13_out, Ai);
  or or_7 (or_7_out, and_14_out, and_15_out, Ai, and_16_out);
  and and_20 (a, Enable, or_2_out);
  and and_21 (d, Enable, or_4_out);
  and and_22 (f, Enable, or_6_out);
  and and_23 (g, Enable, or_7_out);
endmodule

module Calc_Countdown (
  input  C5,
  input  C4,
  input  C3,
  input  C2,
  input  C1,
  input  C0,
  output T2,
  output T1,
  output T0,
  output G3,
  output G2,
  output G1,
  output G0
);

  wire and_2_out, and_3_out, and_4_out, and_5_out, and_6_out, and_7_out, and_8_out, and_9_out, and_10_out,
       and_11_out, and_12_out, and_13_out, and_14_out, and_15_out, and_16_out, and_17_out, and_18_out,
       and_19_out, and_20_out, and_21_out, and_22_out, and_23_out, and_24_out, and_25_out, and_26_out,
       and_27_out, and_28_out, and_29_out, and_30_out, and_31_out, and_32_out, and_33_out, and_34_out,
       and_35_out, and_36_out, and_37_out, and_38_out, and_39_out, and_40_out, and_41_out, and_42_out,
       and_43_out, and_44_out, and_45_out, not_1_out, not_2_out, not_3_out, not_4_out, not_5_out, not_6_out;

  not not_1 (not_1_out, C5);
  not not_2 (not_2_out, C4);
  not not_3 (not_3_out, C3);
  not not_4 (not_4_out, C2);
  not not_5 (not_5_out, C1);
  not not_6 (not_6_out, C0);
  and and_1 (T2, not_1_out, not_2_out, not_3_out, not_4_out, not_5_out, not_6_out);
  and and_2 (and_2_out, not_1_out, not_2_out, C3);
  and and_3 (and_3_out, C4, not_3_out, not_4_out);
  and and_4 (and_4_out, not_1_out, not_3_out, C2, not_5_out, not_6_out);
  and and_5 (and_5_out, not_1_out, not_2_out, C0);
  and and_6 (and_6_out, not_1_out, not_2_out, C1);
  and and_7 (and_7_out, not_1_out, not_2_out, not_3_out, C2);
  and and_8 (and_8_out, C4, C3, not_4_out);
  and and_9 (and_9_out, not_1_out, not_2_out, not_3_out, C0);
  and and_10 (and_10_out, not_1_out, not_3_out, C2, C1);
  and and_11 (and_11_out, not_1_out, C3, not_4_out, not_5_out);
  and and_12 (and_12_out, not_1_out, not_2_out, not_4_out, C1, not_6_out);
  and and_13 (and_13_out, C4, C2, not_5_out, C0);
  and and_14 (and_14_out, C4, C3, not_6_out);
  and and_15 (and_15_out, C5, not_3_out, not_4_out, not_5_out, not_6_out);
  and and_16 (and_16_out, not_1_out, not_2_out, not_3_out, not_4_out, not_5_out, C0);
  and and_17 (and_17_out, not_1_out, not_2_out, not_3_out, not_4_out, C1, not_6_out);
  and and_18 (and_18_out, C4, not_3_out, C2, not_5_out, C0);
  and and_19 (and_19_out, C4, not_3_out, C2, C1, not_6_out);
  and and_20 (and_20_out, not_2_out, C3, not_4_out, C1, C0);
  and and_21 (and_21_out, not_2_out, C3, C2, not_5_out, not_6_out);
  and and_22 (and_22_out, C4, C3, C2, C1, C0);
  and and_23 (and_23_out, C5, not_4_out, C0);
  and and_24 (and_24_out, C5, not_4_out, C1);
  and and_25 (and_25_out, not_2_out, not_3_out, not_4_out, C1, C0);
  and and_26 (and_26_out, C4, not_4_out, not_5_out, not_6_out);
  and and_27 (and_27_out, C4, not_3_out, C2, C1, C0);
  and and_28 (and_28_out, C4, C3, not_4_out, not_5_out);
  and and_29 (and_29_out, C4, C3, not_4_out, not_6_out);
  and and_30 (and_30_out, not_2_out, not_3_out, C2, not_5_out, not_6_out);
  and and_31 (and_31_out, not_1_out, not_2_out, C2, not_5_out, C0);
  and and_32 (and_32_out, not_1_out, not_2_out, C2, C1, not_6_out);
  and and_33 (and_33_out, not_2_out, C3, C2, C0);
  and and_34 (and_34_out, C5, not_5_out, C0);
  and and_35 (and_35_out, C5, C1, not_6_out);
  and and_36 (and_36_out, not_1_out, not_2_out, not_3_out, C1, C0);
  and and_37 (and_37_out, not_1_out, not_2_out, not_3_out, C2, not_5_out, not_6_out);
  and and_38 (and_38_out, not_1_out, C3, not_4_out, not_5_out, not_6_out);
  and and_39 (and_39_out, not_2_out, C3, C2, not_5_out, C0);
  and and_40 (and_40_out, not_2_out, C3, C2, C1, not_6_out);
  and and_41 (and_41_out, C4, not_3_out, not_4_out, not_5_out, C0);
  and and_42 (and_42_out, C4, not_3_out, not_4_out, C1, not_6_out);
  and and_43 (and_43_out, C4, C3, not_4_out, C1, C0);
  and and_44 (and_44_out, C4, C3, not_5_out, not_6_out);
  and and_45 (and_45_out, not_1_out, not_3_out, C2, C1, C0);
  or or_1 (T1, and_2_out, and_3_out, and_4_out, and_5_out, and_6_out);
  or or_2 (T0, and_7_out, and_8_out, and_9_out, and_10_out, and_11_out, and_12_out, and_13_out, and_14_out);
  or or_3 (G3, and_15_out, and_16_out, and_17_out, and_18_out, and_19_out, and_20_out, and_21_out, and_22_out);
  or or_4 (G2, and_23_out, and_24_out, and_25_out, and_26_out, and_27_out, and_28_out, and_29_out, and_30_out, and_31_out, and_32_out, and_33_out);
  or or_5 (G1, and_34_out, and_35_out, and_36_out, and_37_out, and_38_out, and_39_out, and_40_out, and_41_out, and_42_out, and_43_out, and_44_out, and_45_out);

  assign G0 = C0;
endmodule

module NSSecond (
  input  x6,
  input  x5,
  input  x4,
  input  x3,
  input  x2,
  input  x1,
  input  x0,
  output [3:0] Tens,
  output [3:0] Ones
);

  wire and_2_out, and_3_out, and_4_out, and_5_out, and_6_out, and_7_out, and_8_out, and_9_out, and_10_out,
       and_11_out, and_12_out, and_13_out, and_14_out, and_15_out, and_16_out, and_17_out, and_18_out,
       and_19_out, and_20_out, and_21_out, and_22_out, and_23_out, and_24_out, and_25_out, and_26_out,
       and_27_out, and_28_out, and_29_out, and_30_out, and_31_out, and_32_out, and_33_out, and_34_out,
       and_35_out, and_36_out, and_37_out, and_38_out, and_39_out, and_40_out, and_41_out, and_42_out,
       and_43_out, and_44_out, and_45_out, and_46_out, and_47_out, and_48_out, and_49_out, and_50_out,
       and_51_out, and_52_out, and_53_out, and_54_out, and_55_out, and_56_out, and_57_out, and_58_out,
       and_59_out, and_60_out, and_61_out, and_62_out, and_63_out, and_64_out, and_65_out, and_66_out,
       and_67_out, and_68_out, and_69_out, and_70_out, and_71_out, and_72_out, and_73_out, and_74_out,
       and_75_out, not_1_out, not_2_out, not_3_out, not_4_out, not_5_out, not_6_out, not_7_out;

  not not_1 (not_1_out, x6);
  not not_2 (not_2_out, x5);
  not not_3 (not_3_out, x4);
  not not_4 (not_4_out, x3);
  not not_5 (not_5_out, x2);
  not not_6 (not_6_out, x1);
  not not_7 (not_7_out, x0);
  and and_1 (Tens[2], not_1_out, not_2_out, not_3_out, not_4_out, not_5_out, not_6_out, not_7_out);
  and and_2 (and_2_out, not_1_out, not_2_out, not_3_out, x3);
  and and_3 (and_3_out, not_1_out, not_3_out, x3, x0);
  and and_4 (and_4_out, not_1_out, not_3_out, x3, x1);
  and and_5 (and_5_out, not_1_out, not_3_out, x3, x2);
  and and_6 (and_6_out, not_1_out, x5, x4, not_4_out);
  and and_7 (and_7_out, not_1_out, x4, not_4_out, not_5_out);
  and and_8 (and_8_out, not_1_out, not_2_out, not_4_out, x2, not_6_out, not_7_out);
  and and_9 (and_9_out, not_1_out, not_2_out, not_3_out, x0);
  and and_10 (and_10_out, not_1_out, not_2_out, not_3_out, x1);
  and and_11 (and_11_out, x6, not_2_out, not_3_out, not_4_out, not_5_out, not_6_out);
  and and_12 (and_12_out, not_1_out, not_2_out, not_3_out, not_4_out, x2);
  and and_13 (and_13_out, not_1_out, x4, x3, not_5_out);
  and and_14 (and_14_out, not_1_out, x5, x3, x2, not_6_out);
  and and_15 (and_15_out, not_1_out, x5, x4, x3);
  and and_16 (and_16_out, not_1_out, not_2_out, not_3_out, not_4_out, x0);
  and and_17 (and_17_out, not_1_out, not_2_out, not_3_out, not_4_out, x1);
  and and_18 (and_18_out, not_1_out, not_2_out, not_4_out, x2, x0);
  and and_19 (and_19_out, not_1_out, x3, not_5_out, not_6_out, x0);
  and and_20 (and_20_out, not_1_out, not_2_out, x3, not_5_out, not_7_out);
  and and_21 (and_21_out, not_1_out, x5, x3, not_5_out, x1);
  and and_22 (and_22_out, not_1_out, x4, x3, not_6_out);
  and and_23 (and_23_out, not_1_out, not_2_out, x4, x2, x1, not_7_out);
  and and_24 (and_24_out, not_1_out, x5, not_3_out, not_4_out, not_5_out, not_6_out, not_7_out);
  and and_25 (and_25_out, not_1_out, not_2_out, not_3_out, not_4_out, not_5_out, not_6_out, x0);
  and and_26 (and_26_out, not_2_out, not_3_out, not_4_out, not_5_out, x1, not_7_out);
  and and_27 (and_27_out, x6, not_2_out, not_3_out, not_4_out, not_5_out, x1);
  and and_28 (and_28_out, not_1_out, not_2_out, not_3_out, x3, not_5_out, x1, x0);
  and and_29 (and_29_out, not_1_out, not_2_out, not_3_out, x3, x2, not_6_out, not_7_out);
  and and_30 (and_30_out, not_1_out, x5, not_3_out, x3, x2, x1);
  and and_31 (and_31_out, not_1_out, not_2_out, x4, not_4_out, x2, not_6_out, x0);
  and and_32 (and_32_out, not_1_out, not_2_out, x4, not_4_out, x2, x1, not_7_out);
  and and_33 (and_33_out, not_1_out, x5, x4, x3, not_5_out, not_6_out);
  and and_34 (and_34_out, not_1_out, not_2_out, x4, x3, x2, x1, x0);
  and and_35 (and_35_out, not_1_out, not_3_out, not_4_out, not_5_out, x1, x0);
  and and_36 (and_36_out, x6, not_2_out, not_3_out, not_4_out, x2);
  and and_37 (and_37_out, x6, not_2_out, not_3_out, x2, not_6_out, not_7_out);
  and and_38 (and_38_out, not_1_out, not_2_out, x4, not_4_out, x2, x1, x0);
  and and_39 (and_39_out, not_1_out, not_2_out, x4, x3, not_5_out, not_6_out);
  and and_40 (and_40_out, not_1_out, x5, not_4_out, not_5_out, x1);
  and and_41 (and_41_out, not_1_out, not_3_out, not_4_out, x2, not_6_out, not_7_out);
  and and_42 (and_42_out, not_1_out, x5, not_3_out, not_5_out, not_6_out, x0);
  and and_43 (and_43_out, not_1_out, x5, x4, not_5_out, x1);
  and and_44 (and_44_out, not_1_out, x5, x4, x3, x2, not_6_out);
  and and_45 (and_45_out, not_1_out, not_2_out, not_3_out, x2, not_6_out, x0);
  and and_46 (and_46_out, not_1_out, not_2_out, not_3_out, x2, x1, not_7_out);
  and and_47 (and_47_out, not_1_out, x4, not_4_out, not_5_out, not_6_out, not_7_out);
  and and_48 (and_48_out, not_1_out, x5, x4, not_4_out, not_5_out);
  and and_49 (and_49_out, not_1_out, not_2_out, x4, x3, not_5_out, not_7_out);
  and and_50 (and_50_out, not_1_out, not_2_out, not_3_out, x3, x2, x0);
  and and_51 (and_51_out, not_1_out, not_2_out, not_3_out, not_4_out, x1, x0);
  and and_52 (and_52_out, not_2_out, not_3_out, not_4_out, x2, not_6_out, not_7_out);
  and and_53 (and_53_out, not_2_out, not_3_out, x3, x2, not_6_out, x0);
  and and_54 (and_54_out, not_2_out, not_3_out, x3, x2, x1, not_7_out);
  and and_55 (and_55_out, not_1_out, x4, not_4_out, not_5_out, not_6_out, x0);
  and and_56 (and_56_out, not_1_out, not_2_out, x4, not_4_out, not_5_out, x1, not_7_out);
  and and_57 (and_57_out, not_1_out, not_2_out, not_4_out, x2, x1, x0);
  and and_58 (and_58_out, not_1_out, x4, x3, not_5_out, x1, x0);
  and and_59 (and_59_out, not_1_out, not_2_out, x4, x3, not_6_out, not_7_out);
  and and_60 (and_60_out, not_1_out, x5, not_4_out, not_6_out, x0);
  and and_61 (and_61_out, not_1_out, x5, not_3_out, not_4_out, x1, not_7_out);
  and and_62 (and_62_out, not_1_out, x5, x3, not_5_out, x1);
  and and_63 (and_63_out, not_1_out, x5, x4, not_4_out, not_6_out);
  and and_64 (and_64_out, not_1_out, x5, x4, x3, x1);
  and and_65 (and_65_out, not_2_out, not_3_out, x3, not_5_out, not_6_out, not_7_out);
  and and_66 (and_66_out, x6, not_2_out, not_3_out, x3, not_5_out, not_6_out);
  and and_67 (and_67_out, x6, not_2_out, not_3_out, not_4_out, x2, not_6_out);
  and and_68 (and_68_out, x6, not_2_out, not_3_out, not_4_out, not_7_out);
  and and_69 (and_69_out, x6, not_2_out, not_3_out, not_5_out, not_7_out);
  and and_70 (and_70_out, not_1_out, not_2_out, x0);
  and and_71 (and_71_out, not_2_out, not_3_out, x3, x2, x0);
  and and_72 (and_72_out, not_1_out, not_3_out, not_4_out, x0);
  and and_73 (and_73_out, not_1_out, x5, x3, x1, not_7_out);
  and and_74 (and_74_out, not_1_out, x5, x3, x2, not_7_out);
  and and_75 (and_75_out, not_1_out, x5, x4, not_7_out);
  or or_1 (Tens[1], and_2_out, and_3_out, and_4_out, and_5_out, and_6_out, and_7_out, and_8_out, and_9_out, and_10_out);
  or or_2 (Tens[0], and_11_out, and_12_out, and_13_out, and_14_out, and_15_out, and_16_out, and_17_out, and_18_out, and_19_out, and_20_out, and_21_out, and_22_out, and_23_out);
  or or_3 (Ones[3], and_24_out, and_25_out, and_26_out, and_27_out, and_28_out, and_29_out, and_30_out, and_31_out, and_32_out, and_33_out, and_34_out);
  or or_4 (Ones[2], and_35_out, and_36_out, and_37_out, and_38_out, and_39_out, and_40_out, and_41_out, and_42_out, and_43_out, and_44_out, and_45_out, and_46_out, and_47_out, and_48_out, and_49_out, and_50_out);
  or or_5 (Ones[1], and_51_out, and_52_out, and_53_out, and_54_out, and_55_out, and_56_out, and_57_out, and_58_out, and_59_out, and_60_out, and_61_out, and_62_out, and_63_out, and_64_out, and_65_out, and_66_out, and_67_out);
  or or_6 (Ones[0], and_68_out, and_69_out, and_70_out, and_71_out, and_72_out, and_73_out, and_74_out, and_75_out);

  assign Tens[3] = 1'b0;
endmodule

module EWSecond (
  input  x6,
  input  x5,
  input  x4,
  input  x3,
  input  x2,
  input  x1,
  input  x0,
  output [3:0] Tens,
  output [3:0] Ones
);

  wire and_2_out, and_3_out, and_4_out, and_5_out, and_6_out, and_7_out, and_8_out, and_9_out, and_10_out,
       and_11_out, and_12_out, and_13_out, and_14_out, and_15_out, and_16_out, and_17_out, and_18_out,
       and_19_out, and_20_out, and_21_out, and_22_out, and_23_out, and_24_out, and_25_out, and_26_out,
       and_27_out, and_28_out, and_29_out, and_30_out, and_31_out, and_32_out, and_33_out, and_34_out,
       and_35_out, and_36_out, and_37_out, and_38_out, and_39_out, and_40_out, and_41_out, and_42_out,
       and_43_out, and_44_out, and_45_out, and_46_out, and_47_out, and_48_out, and_49_out, and_50_out,
       and_51_out, and_52_out, and_53_out, and_54_out, and_55_out, and_56_out, and_57_out, and_58_out,
       and_59_out, and_60_out, and_61_out, and_62_out, and_63_out, and_64_out, and_65_out, and_66_out,
       and_67_out, not_1_out, not_2_out, not_3_out, not_4_out, not_5_out, not_6_out, not_7_out;

  not not_1 (not_1_out, x6);
  not not_2 (not_2_out, x5);
  not not_3 (not_3_out, x4);
  not not_4 (not_4_out, x3);
  not not_5 (not_5_out, x2);
  not not_6 (not_6_out, x1);
  not not_7 (not_7_out, x0);
  and and_1 (Tens[2], not_1_out, x5, not_3_out, x3, not_5_out, not_6_out, x0);
  and and_2 (and_2_out, not_1_out, not_2_out, not_3_out);
  and and_3 (and_3_out, not_1_out, x5, x4, not_4_out);
  and and_4 (and_4_out, not_1_out, x4, not_4_out, not_5_out, not_6_out, not_7_out);
  and and_5 (and_5_out, not_1_out, x5, x4, not_5_out);
  and and_6 (and_6_out, not_1_out, x5, x3, x2, not_6_out);
  and and_7 (and_7_out, not_1_out, not_3_out, x3, x1);
  and and_8 (and_8_out, x6, not_2_out, not_3_out, not_4_out);
  and and_9 (and_9_out, not_1_out, x5, not_3_out, x3, x1);
  and and_10 (and_10_out, not_1_out, x5, not_3_out, x3, x2);
  and and_11 (and_11_out, not_1_out, x5, x4, not_4_out, not_5_out);
  and and_12 (and_12_out, not_1_out, x5, x3, x2, x1);
  and and_13 (and_13_out, not_1_out, not_2_out, not_4_out, not_5_out, x0);
  and and_14 (and_14_out, not_2_out, not_3_out, not_4_out, not_6_out);
  and and_15 (and_15_out, not_2_out, not_3_out, not_4_out, not_7_out);
  and and_16 (and_16_out, not_1_out, not_2_out, x4, not_4_out, x2);
  and and_17 (and_17_out, not_1_out, not_2_out, x4, x3, not_5_out, not_6_out);
  and and_18 (and_18_out, not_1_out, not_2_out, x4, not_5_out, x1, not_7_out);
  and and_19 (and_19_out, not_1_out, not_2_out, not_3_out, not_4_out, x2, x1, x0);
  and and_20 (and_20_out, not_2_out, not_3_out, x3, not_5_out, not_6_out, not_7_out);
  and and_21 (and_21_out, x6, not_2_out, not_3_out, x3, not_5_out, not_6_out);
  and and_22 (and_22_out, not_1_out, x5, not_3_out, x3, not_5_out, x1);
  and and_23 (and_23_out, not_1_out, not_2_out, x4, not_4_out, not_5_out, not_6_out, x0);
  and and_24 (and_24_out, not_1_out, not_2_out, x4, not_4_out, not_5_out, x1, not_7_out);
  and and_25 (and_25_out, not_1_out, x5, x4, not_4_out, x2, not_6_out);
  and and_26 (and_26_out, not_1_out, not_2_out, x4, x3, not_5_out, x1, x0);
  and and_27 (and_27_out, not_1_out, not_2_out, x4, x3, x2, not_6_out, not_7_out);
  and and_28 (and_28_out, not_1_out, x5, x4, x3, x2, x1);
  and and_29 (and_29_out, x6, not_2_out, not_3_out, x3, x2, not_6_out);
  and and_30 (and_30_out, not_1_out, not_2_out, x4, not_4_out, not_5_out, x1, x0);
  and and_31 (and_31_out, not_1_out, x5, not_3_out, x2, not_6_out);
  and and_32 (and_32_out, not_1_out, x5, not_3_out, x3, x2);
  and and_33 (and_33_out, not_1_out, x5, x4, not_4_out, x2, x1);
  and and_34 (and_34_out, not_1_out, x5, x4, x3, not_5_out, not_6_out);
  and and_35 (and_35_out, not_1_out, not_3_out, not_4_out, not_5_out, not_6_out, not_7_out);
  and and_36 (and_36_out, x6, not_2_out, not_3_out, not_4_out, not_5_out);
  and and_37 (and_37_out, not_1_out, not_2_out, x4, not_4_out, x2, not_6_out);
  and and_38 (and_38_out, not_1_out, not_2_out, not_3_out, not_5_out, not_6_out, x0);
  and and_39 (and_39_out, not_2_out, not_3_out, not_5_out, x1, not_7_out);
  and and_40 (and_40_out, not_2_out, not_3_out, x3, not_5_out, x1);
  and and_41 (and_41_out, not_1_out, not_3_out, x3, x2, not_6_out, not_7_out);
  and and_42 (and_42_out, not_1_out, not_2_out, x4, x2, x1, not_7_out);
  and and_43 (and_43_out, not_1_out, not_2_out, x4, x3, x2, x0);
  and and_44 (and_44_out, not_2_out, not_3_out, not_4_out, not_6_out, not_7_out);
  and and_45 (and_45_out, x6, not_2_out, not_3_out, not_4_out, not_6_out);
  and and_46 (and_46_out, not_1_out, not_2_out, not_4_out, not_5_out, x1, x0);
  and and_47 (and_47_out, not_1_out, not_2_out, not_3_out, x3, not_6_out, x0);
  and and_48 (and_48_out, not_2_out, not_3_out, x3, x1, not_7_out);
  and and_49 (and_49_out, x6, not_2_out, not_3_out, x3, x1);
  and and_50 (and_50_out, not_1_out, not_2_out, not_4_out, x2, not_6_out, not_7_out);
  and and_51 (and_51_out, not_1_out, not_2_out, x4, x3, not_5_out, not_6_out, not_7_out);
  and and_52 (and_52_out, not_1_out, not_2_out, x3, x2, not_6_out, x0);
  and and_53 (and_53_out, not_1_out, not_2_out, x3, x2, x1, not_7_out);
  and and_54 (and_54_out, not_1_out, x5, not_4_out, not_5_out, not_6_out, x0);
  and and_55 (and_55_out, not_1_out, x5, not_3_out, not_4_out, x1, not_7_out);
  and and_56 (and_56_out, not_1_out, x5, not_4_out, x2, x1);
  and and_57 (and_57_out, not_1_out, x5, not_3_out, x3, x2, not_6_out);
  and and_58 (and_58_out, not_1_out, x5, x4, not_4_out, not_5_out, not_6_out);
  and and_59 (and_59_out, not_1_out, x5, x4, x3, not_5_out, x1);
  and and_60 (and_60_out, not_1_out, not_2_out, x4, not_4_out, x1, x0);
  and and_61 (and_61_out, x6, not_2_out, not_3_out, not_7_out);
  and and_62 (and_62_out, not_1_out, not_2_out, x0);
  and and_63 (and_63_out, x6, not_2_out, not_4_out, not_5_out, not_6_out, not_7_out);
  and and_64 (and_64_out, not_1_out, not_3_out, not_4_out, not_5_out, x0);
  and and_65 (and_65_out, not_1_out, x5, x2, not_7_out);
  and and_66 (and_66_out, not_1_out, x5, x3, not_7_out);
  and and_67 (and_67_out, not_1_out, x5, x4, not_7_out);
  or or_1 (Tens[1], and_2_out, and_3_out, and_4_out, and_5_out, and_6_out, and_7_out);
  or or_2 (Tens[0], and_8_out, and_9_out, and_10_out, and_11_out, and_12_out, and_13_out, and_14_out, and_15_out, and_16_out, and_17_out, and_18_out);
  or or_3 (Ones[3], and_19_out, and_20_out, and_21_out, and_22_out, and_23_out, and_24_out, and_25_out, and_26_out, and_27_out, and_28_out);
  or or_4 (Ones[2], and_29_out, and_30_out, and_31_out, and_32_out, and_33_out, and_34_out, and_35_out, and_36_out, and_37_out, and_38_out, and_39_out, and_40_out, and_41_out, and_42_out, and_43_out);
  or or_5 (Ones[1], and_44_out, and_45_out, and_46_out, and_47_out, and_48_out, and_49_out, and_50_out, and_51_out, and_52_out, and_53_out, and_54_out, and_55_out, and_56_out, and_57_out, and_58_out, and_59_out, and_60_out);
  or or_6 (Ones[0], and_61_out, and_62_out, and_63_out, and_64_out, and_65_out, and_66_out, and_67_out);

  assign Tens[3] = 1'b0;
endmodule
